# Fritzing sketch w3_leds_and_button_pulldown (saved by Fritzing 1.0.3)
breadboards: 1

parts:
  Arduino1 = Arduino Uno (Rev3)
  R1 = Resistor [resistance=220 power=0.25W package=THT]
  LED1 = LED - 5mm [color="Red (633nm)" package="5 mm [THT]"]
  R2 = Resistor [resistance=220 power=0.25W package=THT]
  LED2 = LED - 5mm [color="Red (633nm)" package="5 mm [THT]"]
  SW1 = Pushbutton [package="[THT]"]
  Rpulldown = Resistor [resistance=10k power=0.25W package=THT]

nets:
  N1: Arduino1.D9_PWM, R1.Pin_0
  N2: Arduino1.D10_PWM/SS, R2.Pin_0
  N3: Arduino1.D2, Arduino1.5V, SW1.Pin_1, SW1.Pin_2, Rpulldown.Pin_0
  N4: Arduino1.GND, LED2.cathode, Rpulldown.Pin_1
  N5: R1.Pin_1, LED1.anode
  N6: R2.Pin_1, LED2.anode
  N7: SW1.Pin_3, SW1.Pin_4
