# Fritzing sketch w4_three_leds_chasing (saved by Fritzing 1.0.3)
breadboards: 1

parts:
  Arduino1 = Arduino Uno (Rev3)
  R1 = Resistor [resistance=220 power=0.25W package=THT]
  LED1 = LED - 5mm [color="Red (633nm)" package="5 mm [THT]"]
  R2 = Resistor [resistance=220 power=0.25W package=THT]
  LED2 = LED - 5mm [color="Red (633nm)" package="5 mm [THT]"]
  R3 = Resistor [resistance=220 power=0.25W package=THT]
  LED3 = LED - 5mm [color="Red (633nm)" package="5 mm [THT]"]

nets:
  N1: Arduino1.D9_PWM, R1.Pin_0
  N2: Arduino1.D10_PWM/SS, R2.Pin_0
  N3: Arduino1.D11_PWM/MOSI, R3.Pin_0
  N4: Arduino1.GND, LED2.cathode, LED3.cathode
  N5: R1.Pin_1, LED1.anode
  N6: R2.Pin_1, LED2.anode
  N7: R3.Pin_1, LED3.anode
