# Fritzing sketch w_p2_04_two_buttons_variant (saved by Fritzing 1.0.3)
breadboards: 1

parts:
  Arduino1 = Arduino Uno (Rev3)
  R1 = Resistor [resistance=220 power=0.25W package=THT]
  LED1 = LED - 5mm [color="Red (633nm)" package="5 mm [THT]"]
  SW1 = Pushbutton [package="[THT]"]
  Rpulldown = Resistor [resistance=10k power=0.25W package=THT]
  BUZZER = Buzzer 12mm [package=buzzer-12mm-ns-kit]  # not connected
  SW2 = Round Pushbutton  # not connected
  Rpulldown2 = Resistor [Resistance=220 power=0.25W resistance=10k package=THT]  # not connected

nets:
  N1: Arduino1.D9_PWM, R1.Pin_0
  N2: Arduino1.D2, Arduino1.5V, SW1.Pin_1, SW1.Pin_2, Rpulldown.Pin_0
  N3: Arduino1.GND, Rpulldown.Pin_1
  N4: R1.Pin_1, LED1.anode
  N5: SW1.Pin_3, SW1.Pin_4
