# Fritzing sketch w_p3_03_hcsr04_led_buzzer (saved by Fritzing 1.0.3)
breadboards: 1

parts:
  Arduino1 = Arduino Uno (Rev3)
  R1 = Resistor [resistance=220 power=0.25W package=THT]
  LED1 = LED - 5mm [color="Red (633nm)" package="5 mm [THT]"]
  HC-SR04 = HC-SR04 Ultrasonic Distance Sensor  # not connected
  BUZZER = Buzzer 12mm [package=buzzer-12mm-ns-kit]  # not connected

nets:
  N1: Arduino1.D9_PWM, R1.Pin_0
  N2: Arduino1.GND, LED1.cathode
  N3: R1.Pin_1, LED1.anode
