# Fritzing sketch w_p3_04_two_stage (saved by Fritzing 1.0.3)
breadboards: 1

parts:
  Arduino1 = Arduino Uno (Rev3)
  R1 = Resistor [resistance=220 power=0.25W package=THT]
  LED1 = LED - 5mm [color="Red (633nm)" package="5 mm [THT]"]
  R2 = Resistor [resistance=220 power=0.25W package=THT]
  LED2 = LED - 5mm [color="Red (633nm)" package="5 mm [THT]"]
  HC-SR04 = HC-SR04 Ultrasonic Distance Sensor  # not connected
  BUZZER = Buzzer 12mm [package=buzzer-12mm-ns-kit]  # not connected

nets:
  N1: Arduino1.D9_PWM, R1.Pin_0
  N2: Arduino1.D10_PWM/SS, R2.Pin_0
  N3: Arduino1.GND, LED2.cathode
  N4: R1.Pin_1, LED1.anode
  N5: R2.Pin_1, LED2.anode
