# Fritzing sketch w_p4_05_button_tier3 (saved by Fritzing 1.0.3)
breadboards: 1

parts:
  Arduino1 = Arduino Uno (Rev3)
  SW1 = Pushbutton [package="[THT]"]
  Rpulldown = Resistor [resistance=10k power=0.25W package=THT]

nets:
  N1: Arduino1.D2, Arduino1.5V, SW1.Pin_1, SW1.Pin_2, Rpulldown.Pin_0
  N2: Arduino1.GND, Rpulldown.Pin_1
  N3: SW1.Pin_3, SW1.Pin_4
